# Fritzing sketch Shematic (saved by Fritzing 0.9.3b)

parts:
  Part1 = Arduino Mega 2560 (Rev3)
  HLK-PM1 = HLK-PM12 [part_number=HLK-PM12]
  HC-SR04_Sensor_1 = HC-SR04 Ultrasonic Distance Sensor
  M1 = MakerFocus MAX30102
  Mod1 = gy-906
  Load_Cell2 = Load Cell - Red/white/black/green
  Part2 = HX711 Weighing Sensor Module
  Load_Cell3 = Load Cell - Red/white/black/green
  HLK-PM2 = HLK-PM01

nets:
  N1: Part1.D21/SCL, M1.SCL, Mod1.SCL
  N2: Part1.D20/SDA, M1.SDA, Mod1.SDA
  GND: Part1.GND, HLK-PM1.-Vo, HC-SR04_Sensor_1.GND, M1.GND, Mod1.GND, Part2.GND, HLK-PM2.-Vo
  N3: Part1.VIN, HLK-PM1.+Vo
  N4: Part1.D22, Part2.CK/TX
  N5: Part1.D23, Part2.DO/RX
  N6: Part1.D24, HC-SR04_Sensor_1.TRIG
  N7: Part1.D25, HC-SR04_Sensor_1.ECHO
  VCC: HC-SR04_Sensor_1.VCC, M1.VIN, Mod1.VIN, Part2.VCC, HLK-PM2.+Vo
  N8: Load_Cell2.wire1, Part2.E+, Load_Cell3.wire1
  N9: Load_Cell2.wire2, Part2.A+, Load_Cell3.wire2
  N10: Load_Cell2.wire3, Part2.E-, Load_Cell3.wire3
  N11: Load_Cell2.wire4, Part2.A-, Load_Cell3.wire4

notes:
  Power Supply
  Input : AC 220V
  Output : 5V / 3.3V
  HC-SR04 Ultrasonic
  VCC
  5V
  Power
  GND
  GND
  Ground
  TRIG
  24
  Trigger
  ECHO
  25
  Echo
  MAX30102
  VIN 3.3V Power
  GND
  GND
  Ground
  SDA
  20 (SDA)
  I²C Data
  SCL
  21 (SCL)
  I²C Clock
  MLX90614
  VIN 3.3V Power
  GND
  GND
  Ground
  SDA
  20 (SDA)
  I²C Data
  SCL
  21 (SCL)
  I²C Clock
  H7011
  VCC
  5V
  Power
  GND
  GND
  Ground
  DT / DOUT
  22
  Data
  SCK / CLK
  23
  Clock
  Power Supply
  Input : AC 220V
  Output : 12V
  Connected To Computer

custom parts:
  MakerFocus MAX30102: Oximeter module using the MAX30102 chip. As usual, if you want the mounting holes in pcb, you need to drag a hole over the pad in silkscreen to actually drill the hole (by default they are not drilled)
  gy-906: gy-906 Non-contact PIR I2C interface temperature sensor breakout board.
  Load Cell - Red/white/black/green: A rectangle load cell/weighting pressure Sensor with four wires - Red, white, black, green. Normally corresponding with E+, E-, A+, A- respectively.
  HX711 Weighing Sensor Module: HX711 is a precision 24-bit analog-to-digital converter (ADC) designed for weigh scales and industrial control applications to interface directly with a bridge sensor.
